# Fritzing sketch ValveControllerPCB (saved by Fritzing 0.9.4)
breadboards: 2

parts:
  ESP32 = ESP32-38PinWide [part_number=ESP32-38PinWide]
  Multiplexer = Analog Digital MUX Breakout
  U2 = 16-Channel Relay Module [package=relay-16ch]
  Bauteil1 = TXB0108 8-channel Bi-directional Logic Level Converter
  Bauteil2 = TXB0108 8-channel Bi-directional Logic Level Converter

nets:
  N1: ESP32.3.3, Bauteil1.OE, Bauteil1.VCCA, Bauteil2.OE, Bauteil2.VCCA
  N2: ESP32.GPIO33, Multiplexer.SIG
  N3: ESP32.GPIO25, Multiplexer.S3
  N4: ESP32.GPIO26, Multiplexer.S2
  N5: ESP32.GPIO27, Multiplexer.S1
  N6: ESP32.GPIO14, Multiplexer.S0
  N7: ESP32.GPIO12, Multiplexer.EN
  GND: ESP32.GND, Multiplexer.GND, U2.OUT_GND, Bauteil1.GND, Bauteil2.GND
  VIN: ESP32.VIN, Multiplexer.VCC, Bauteil1.VCCB, Bauteil2.VCCB
  N8: Multiplexer.C0, Bauteil1.A1
  N9: Multiplexer.C1, Bauteil1.A2
  N10: Multiplexer.C2, Bauteil1.A3
  N11: Multiplexer.C3, Bauteil1.A4
  N12: Multiplexer.C4, Bauteil1.A5
  N13: Multiplexer.C5, Bauteil1.A6
  N14: Multiplexer.C6, Bauteil1.A7
  N15: Multiplexer.C7, Bauteil1.A8
  N16: Multiplexer.C8, Bauteil2.A1
  N17: Multiplexer.C9, Bauteil2.A2
  N18: Multiplexer.C10, Bauteil2.A3
  N19: Multiplexer.C11, Bauteil2.A4
  N20: Multiplexer.C12, Bauteil2.A5
  N21: Multiplexer.C13, Bauteil2.A6
  N22: Multiplexer.C14, Bauteil2.A7
  N23: Multiplexer.C15, Bauteil2.A8
  N24: U2.IN1, Bauteil1.B1
  N25: U2.IN2, Bauteil1.B2
  N26: U2.IN3, Bauteil1.B3
  N27: U2.IN4, Bauteil1.B4
  N28: U2.IN5, Bauteil1.B5
  N29: U2.IN6, Bauteil1.B6
  N30: U2.IN7, Bauteil1.B7
  N31: U2.IN8, Bauteil1.B8
  N32: U2.IN9, Bauteil2.B1
  N33: U2.IN10, Bauteil2.B2
  N34: U2.IN11, Bauteil2.B3
  N35: U2.IN12, Bauteil2.B4
  N36: U2.IN13, Bauteil2.B5
  N37: U2.IN14, Bauteil2.B6
  N38: U2.IN15, Bauteil2.B7
  N39: U2.IN16, Bauteil2.B8

custom parts:
  ESP32-38PinWide: Generic 38-Pin ESP32 with wide format (only access to one side of pins on a breadboard) based on Stephen Lilley's HiLetgo ESP-WROOM-32 ESP32 ESP-32S Development Board.
  16-Channel Relay Module: 16 channel relay module
  TXB0108 8-channel Bi-directional Logic Level Converter: Because the Arduino (and Basic Stamp) are 5V devices, and most modern sensors, displays, flash cards and modes are 3.3V-only, many makers find that they need to perform level shifting/conversion to protect the 3.3V device from 5V. Although one can use resistors to make a divider, for high speed transfers, the resistors can add a lot of slew and cause havoc that is tough to debug. For that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
