# Fritzing sketch ValveControllerPCB_ver1 (saved by Fritzing 0.9.4)
circuit board: 7.08451cm x 8.67585cm
breadboards: 3

parts:
  Multiplexer = Analog Digital MUX Breakout
  Logic_Level_Converter_1 = TXB0108 8-channel Bi-directional Logic Level Converter
  Logic_Level_Converter2 = TXB0108 8-channel Bi-directional Logic Level Converter
  J1 = female pin header, 10 pins [form="♀ (female)"]
  J2 = female pin header, 10 pins [form="♀ (female)"]
  ESP32 = ESP32-38PinWide [part_number=ESP32-38PinWide]

nets:
  N1: Multiplexer.C0, Logic_Level_Converter_1.A1
  N2: Multiplexer.C1, Logic_Level_Converter_1.A2
  N3: Multiplexer.C2, Logic_Level_Converter_1.A3
  N4: Multiplexer.C3, Logic_Level_Converter_1.A4
  N5: Multiplexer.C4, Logic_Level_Converter_1.A5
  N6: Multiplexer.C5, Logic_Level_Converter_1.A6
  N7: Multiplexer.C6, Logic_Level_Converter_1.A7
  N8: Multiplexer.C7, Logic_Level_Converter_1.A8
  N9: Multiplexer.C8, Logic_Level_Converter2.A1
  N10: Multiplexer.C9, Logic_Level_Converter2.A2
  N11: Multiplexer.C10, Logic_Level_Converter2.A3
  N12: Multiplexer.C11, Logic_Level_Converter2.A4
  N13: Multiplexer.C12, Logic_Level_Converter2.A5
  N14: Multiplexer.C13, Logic_Level_Converter2.A6
  N15: Multiplexer.C14, Logic_Level_Converter2.A7
  N16: Multiplexer.C15, Logic_Level_Converter2.A8
  GND: Multiplexer.GND, Logic_Level_Converter_1.GND, Logic_Level_Converter2.GND, J1.pin10, ESP32.GND
  VCC: Multiplexer.VCC, Logic_Level_Converter_1.VCCB, Logic_Level_Converter2.VCCB, ESP32.VIN
  N17: Multiplexer.EN, ESP32.GPIO12
  N18: Multiplexer.S0, ESP32.GPIO14
  N19: Multiplexer.S1, ESP32.GPIO27
  N20: Multiplexer.S2, ESP32.GPIO26
  N21: Multiplexer.S3, ESP32.GPIO25
  N22: Multiplexer.SIG, ESP32.GPIO33
  N23: Logic_Level_Converter_1.B1, J2.pin2
  N24: Logic_Level_Converter_1.B2, J2.pin3
  N25: Logic_Level_Converter_1.B3, J2.pin4
  N26: Logic_Level_Converter_1.B4, J2.pin5
  N27: Logic_Level_Converter_1.B5, J2.pin6
  N28: Logic_Level_Converter_1.B6, J2.pin7
  N29: Logic_Level_Converter_1.B7, J2.pin8
  N30: Logic_Level_Converter_1.B8, J2.pin9
  N31: Logic_Level_Converter_1.OE, Logic_Level_Converter_1.VCCA, Logic_Level_Converter2.OE, Logic_Level_Converter2.VCCA, ESP32.3.3
  N32: Logic_Level_Converter2.B1, J1.pin2
  N33: Logic_Level_Converter2.B2, J1.pin3
  N34: Logic_Level_Converter2.B3, J1.pin4
  N35: Logic_Level_Converter2.B4, J1.pin5
  N36: Logic_Level_Converter2.B5, J1.pin6
  N37: Logic_Level_Converter2.B6, J1.pin7
  N38: Logic_Level_Converter2.B7, J1.pin8
  N39: Logic_Level_Converter2.B8, J1.pin9

custom parts:
  TXB0108 8-channel Bi-directional Logic Level Converter: Because the Arduino (and Basic Stamp) are 5V devices, and most modern sensors, displays, flash cards and modes are 3.3V-only, many makers find that they need to perform level shifting/conversion to protect the 3.3V device from 5V. Although one can use resistors to make a divider, for high speed transfers, the resistors can add a lot of slew and cause havoc that is tough to debug. For that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
  ESP32-38PinWide: Generic 38-Pin ESP32 with wide format (only access to one side of pins on a breadboard) based on Stephen Lilley's HiLetgo ESP-WROOM-32 ESP32 ESP-32S Development Board.
