# Fritzing sketch ValveControllerdoubleESP32PCB_ver2 (saved by Fritzing 0.9.4)
circuit board: 9cm x 9cm
breadboards: 2

parts:
  Logic_Level_Converter_1 = TXB0108 8-channel Bi-directional Logic Level Converter
  Logic_Level_Converter2 = TXB0108 8-channel Bi-directional Logic Level Converter
  J1 = female pin header, 10 pins [form="♀ (female)"]
  J2 = female pin header, 10 pins [form="♀ (female)"]
  ESP32 = ESP32-38PinWide [part_number=ESP32-38PinWide]
  ESP33 = ESP32-38PinWide [part_number=ESP32-38PinWide]

nets:
  N1: Logic_Level_Converter_1.VCCB, ESP33.VIN
  N2: Logic_Level_Converter_1.B1, J2.pin2
  N3: Logic_Level_Converter_1.B2, J2.pin3
  N4: Logic_Level_Converter_1.B3, J2.pin4
  N5: Logic_Level_Converter_1.B4, J2.pin5
  N6: Logic_Level_Converter_1.B5, J2.pin6
  N7: Logic_Level_Converter_1.B6, J2.pin7
  N8: Logic_Level_Converter_1.B7, J2.pin8
  N9: Logic_Level_Converter_1.B8, J2.pin9
  GND: Logic_Level_Converter_1.GND, J2.pin10, ESP33.GND
  N10: Logic_Level_Converter_1.OE, Logic_Level_Converter_1.VCCA, ESP33.3.3
  N11: Logic_Level_Converter_1.A8, ESP33.GPIO13
  N12: Logic_Level_Converter_1.A7, ESP33.GPIO18
  N13: Logic_Level_Converter_1.A6, ESP33.GPIO14
  N14: Logic_Level_Converter_1.A5, ESP33.GPIO27
  N15: Logic_Level_Converter_1.A4, ESP33.GPIO26
  N16: Logic_Level_Converter_1.A3, ESP33.GPIO25
  N17: Logic_Level_Converter_1.A2, ESP33.GPIO33
  N18: Logic_Level_Converter_1.A1, ESP33.GPIO32
  N19: Logic_Level_Converter2.VCCB, ESP32.VIN
  N20: Logic_Level_Converter2.B1, J1.pin2
  N21: Logic_Level_Converter2.B2, J1.pin3
  N22: Logic_Level_Converter2.B3, J1.pin4
  N23: Logic_Level_Converter2.B4, J1.pin5
  N24: Logic_Level_Converter2.B5, J1.pin6
  N25: Logic_Level_Converter2.B6, J1.pin7
  N26: Logic_Level_Converter2.B7, J1.pin8
  N27: Logic_Level_Converter2.B8, J1.pin9
  GND_2: Logic_Level_Converter2.GND, J1.pin10, ESP32.GND
  N28: Logic_Level_Converter2.OE, Logic_Level_Converter2.VCCA, ESP32.3.3
  N29: Logic_Level_Converter2.A8, ESP32.GPIO13
  N30: Logic_Level_Converter2.A7, ESP32.GPIO18
  N31: Logic_Level_Converter2.A6, ESP32.GPIO14
  N32: Logic_Level_Converter2.A5, ESP32.GPIO27
  N33: Logic_Level_Converter2.A4, ESP32.GPIO26
  N34: Logic_Level_Converter2.A3, ESP32.GPIO25
  N35: Logic_Level_Converter2.A2, ESP32.GPIO33
  N36: Logic_Level_Converter2.A1, ESP32.GPIO32

custom parts:
  TXB0108 8-channel Bi-directional Logic Level Converter: Because the Arduino (and Basic Stamp) are 5V devices, and most modern sensors, displays, flash cards and modes are 3.3V-only, many makers find that they need to perform level shifting/conversion to protect the 3.3V device from 5V. Although one can use resistors to make a divider, for high speed transfers, the resistors can add a lot of slew and cause havoc that is tough to debug. For that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
  ESP32-38PinWide: Generic 38-Pin ESP32 with wide format (only access to one side of pins on a breadboard) based on Stephen Lilley's HiLetgo ESP-WROOM-32 ESP32 ESP-32S Development Board.
